// Logisim project AsteroidPong.circ as structural Verilog: 1 circuit, main circuit main
module main (
  input  [4:0] in_1,
  output [31:0] out_2
);

  Multiplexer #(.select(5), .width(32)) multiplexer_1 (
    .in0(32'he0000000), .in1(32'h70000000), .in2(32'h38000000), .in3(32'h1c000000), .in4(32'he000000),
    .in5(32'h7000000), .in6(32'h3800000), .in7(32'h1c00000), .in8(32'he00000), .in9(32'h700000),
    .in10(32'h380000), .in11(32'h1c0000), .in12(32'he0000), .in13(32'h70000), .in14(32'h38000),
    .in15(32'h1c000), .in16(32'he000), .in17(32'h7000), .in18(32'h3800), .in19(32'h1c00), .in20(32'he00),
    .in21(32'h700), .in22(32'h380), .in23(32'h1c0), .in24(32'he0), .in25(32'h70), .in26(32'h38),
    .in27(32'h1c), .in28(32'he), .in29(32'h7), .in30(32'h80000003), .in31(32'hc0000001), .out(out_2),
    .sel(in_1));  // open: en
endmodule
